# Fritzing sketch Base Sketch (saved by Fritzing 0.9.5d)

parts:
  Pro_Micro1 = Pro Micro
  Part1 = InvenSense MPU6050
  U1 = POT [package=alps_pot]
  U2 = POT [package=alps_pot]
  U3 = POT [package=alps_pot]
  U4 = POT [package=alps_pot]

nets:
  N1: Pro_Micro1.D2, Part1.SDA
  N2: Pro_Micro1.D3, Part1.SCL
  N3: Pro_Micro1.D6, U2.S
  N4: Pro_Micro1.D8, U1.S
  N5: Pro_Micro1.D9, U3.S
  N6: Pro_Micro1.D10, U4.S
  VCC: Pro_Micro1.VCC, Part1.VCC, U1.E, U2.E, U3.E, U4.E
  GND: Pro_Micro1.GND, Part1.GND, U1.A, U2.A, U3.A, U4.A

notes:
  Clutch, Brake, Throttle, Steering

custom parts:
  Pro Micro: The SparkFun Pro Micro is a complete USB-based microcontoller development system, in a very small footprint, capable of implementing many types of projects. All programming can be done via the USB port.
